// Logisim project FloatingPointAdder.circ as structural Verilog: 51 circuits, main circuit main
module _1_bit_right_shifter (
  input  [31:0] in_1,
  output [31:0] out_2
);


  assign out_2 = {1'b0, in_1[31:1]};
endmodule

module _2_bit_right_shifter (
  input  [31:0] in_1,
  output [31:0] out_2
);

  wire [31:0] n1_bit_right_shifter_1_out_2;

  _1_bit_right_shifter u_1_bit_right_shifter_1 (.in_1(in_1), .out_2(n1_bit_right_shifter_1_out_2));
  _1_bit_right_shifter u_1_bit_right_shifter_2 (.in_1(n1_bit_right_shifter_1_out_2), .out_2(out_2));
endmodule

module _4_bit_right_shifter (
  input  [31:0] in_1,
  output [31:0] out_2
);

  wire [31:0] n2_bit_right_shifter_1_out_2;

  _2_bit_right_shifter u_2_bit_right_shifter_1 (.in_1(in_1), .out_2(n2_bit_right_shifter_1_out_2));
  _2_bit_right_shifter u_2_bit_right_shifter_2 (.in_1(n2_bit_right_shifter_1_out_2), .out_2(out_2));
endmodule

module _8_bit_right_shifter (
  input  [31:0] in_1,
  output [31:0] out_2
);

  wire [31:0] n4_bit_right_shifter_1_out_2;

  _4_bit_right_shifter u_4_bit_right_shifter_1 (.in_1(in_1), .out_2(n4_bit_right_shifter_1_out_2));
  _4_bit_right_shifter u_4_bit_right_shifter_2 (.in_1(n4_bit_right_shifter_1_out_2), .out_2(out_2));
endmodule

module _16_bit_right_shifter (
  input  [31:0] in_1,
  output [31:0] out_2
);

  wire [31:0] n8_bit_right_shifter_1_out_2;

  _8_bit_right_shifter u_8_bit_right_shifter_1 (.in_1(in_1), .out_2(n8_bit_right_shifter_1_out_2));
  _8_bit_right_shifter u_8_bit_right_shifter_2 (.in_1(n8_bit_right_shifter_1_out_2), .out_2(out_2));
endmodule

module _1_bit_left_shifter (
  input  [31:0] in_1,
  output [31:0] out_2
);


  assign out_2 = {in_1[30:0], 1'b0};
endmodule

module _2_bit_left_shifter (
  input  [31:0] in_1,
  output [31:0] out_2
);

  wire [31:0] n1_bit_left_shifter_1_out_2;

  _1_bit_left_shifter u_1_bit_left_shifter_1 (.in_1(in_1), .out_2(n1_bit_left_shifter_1_out_2));
  _1_bit_left_shifter u_1_bit_left_shifter_2 (.in_1(n1_bit_left_shifter_1_out_2), .out_2(out_2));
endmodule

module _4_bit_left_shifter (
  input  [31:0] in_1,
  output [31:0] out_2
);

  wire [31:0] n2_bit_left_shifter_1_out_2;

  _2_bit_left_shifter u_2_bit_left_shifter_1 (.in_1(in_1), .out_2(n2_bit_left_shifter_1_out_2));
  _2_bit_left_shifter u_2_bit_left_shifter_2 (.in_1(n2_bit_left_shifter_1_out_2), .out_2(out_2));
endmodule

module _8_bit_left_shifter (
  input  [31:0] in_1,
  output [31:0] out_2
);

  wire [31:0] n4_bit_left_shifter_1_out_2;

  _4_bit_left_shifter u_4_bit_left_shifter_1 (.in_1(in_1), .out_2(n4_bit_left_shifter_1_out_2));
  _4_bit_left_shifter u_4_bit_left_shifter_2 (.in_1(n4_bit_left_shifter_1_out_2), .out_2(out_2));
endmodule

module _16_bit_left_shifter (
  input  [31:0] in_1,
  output [31:0] out_2
);

  wire [31:0] n8_bit_left_shifter_1_out_2;

  _8_bit_left_shifter u_8_bit_left_shifter_1 (.in_1(in_1), .out_2(n8_bit_left_shifter_1_out_2));
  _8_bit_left_shifter u_8_bit_left_shifter_2 (.in_1(n8_bit_left_shifter_1_out_2), .out_2(out_2));
endmodule

module _74157 (
  input  _1__S,
  input  _16__Vcc,
  input  _2__A1,
  input  _15__G,
  input  _3__B1,
  input  _14__A4,
  input  _13__B4,
  input  _5__A2,
  input  _6__B2,
  input  _11__A3,
  input  _10__B3,
  input  _8__GND,
  output _4__Y1,
  output _12__Y4,
  output _7__Y2,
  output _9__Y3
);

  wire multiplexer_1_out, multiplexer_2_out, multiplexer_3_out, multiplexer_4_out, not_1_out;

  Multiplexer #(.enable("false")) multiplexer_1 (.in0(_2__A1), .in1(_3__B1), .out(multiplexer_1_out), .sel(_1__S));
  and and_1 (_4__Y1, multiplexer_1_out, not_1_out);
  Multiplexer #(.enable("false")) multiplexer_2 (.in0(_5__A2), .in1(_6__B2), .out(multiplexer_2_out), .sel(_1__S));
  and and_2 (_7__Y2, multiplexer_2_out, not_1_out);
  not not_1 (not_1_out, _15__G);
  Multiplexer #(.enable("false")) multiplexer_3 (.in0(_14__A4), .in1(_13__B4), .out(multiplexer_3_out), .sel(_1__S));
  and and_3 (_12__Y4, multiplexer_3_out, not_1_out);
  Multiplexer #(.enable("false")) multiplexer_4 (.in0(_11__A3), .in1(_10__B3), .out(multiplexer_4_out), .sel(_1__S));
  and and_4 (_9__Y3, multiplexer_4_out, not_1_out);

  // Notes on the sheet:
  //   74157: Quad 2-Line to 1-Line Multiplexer
endmodule

module _4_bit_num_select (
  input  [3:0] in_1,
  input  [3:0] in_2,
  input  in_3,
  output [3:0] out_4
);

  _74157 u_74157_1 (
    ._1__S(in_3), ._2__A1(in_1[0]), ._3__B1(in_2[0]), ._4__Y1(out_4[0]), ._5__A2(in_1[1]), ._6__B2(in_2[1]),
    ._7__Y2(out_4[1]), ._15__G(1'b0), ._14__A4(in_1[3]), ._13__B4(in_2[3]), ._12__Y4(out_4[3]),
    ._11__A3(in_1[2]), ._10__B3(in_2[2]), ._9__Y3(out_4[2]));  // open: _8__GND, _16__Vcc
endmodule

module _8_bit_num_select (
  input  [7:0] in_1,
  input  [7:0] in_2,
  input  in_3,
  output [7:0] out_4
);

  _4_bit_num_select u_4_bit_num_select_1 (.in_1(in_1[3:0]), .in_2(in_2[3:0]), .in_3(in_3), .out_4(out_4[3:0]));
  _4_bit_num_select u_4_bit_num_select_2 (.in_1(in_1[7:4]), .in_2(in_2[7:4]), .in_3(in_3), .out_4(out_4[7:4]));
endmodule

module _16_bit_num_select (
  input  [15:0] in_1,
  input  [15:0] in_2,
  input  in_3,
  output [15:0] out_4
);

  _8_bit_num_select u_8_bit_num_select_1 (.in_1(in_1[7:0]), .in_2(in_2[7:0]), .out_4(out_4[7:0]), .in_3(in_3));
  _8_bit_num_select u_8_bit_num_select_2 (.in_1(in_1[15:8]), .in_2(in_2[15:8]), .out_4(out_4[15:8]), .in_3(in_3));
endmodule

module _32_bit_num_select (
  input  [31:0] in_1,
  input  [31:0] in_2,
  input  in_3,
  output [31:0] out_4
);

  _16_bit_num_select u_16_bit_num_select_1 (.in_1(in_1[15:0]), .in_2(in_2[15:0]), .out_4(out_4[15:0]), .in_3(in_3));
  _16_bit_num_select u_16_bit_num_select_2 (.in_1(in_1[31:16]), .in_2(in_2[31:16]), .out_4(out_4[31:16]), .in_3(in_3));
endmodule

module _1_bit_RS_with_ENB (
  input  [31:0] in_1,
  input  in_2,
  output [31:0] out_3
);

  wire [31:0] n1_bit_right_shifter_1_out_2;

  _1_bit_right_shifter u_1_bit_right_shifter_1 (.in_1(in_1), .out_2(n1_bit_right_shifter_1_out_2));
  _32_bit_num_select u_32_bit_num_select_1 (
    .in_1(in_1), .in_2(n1_bit_right_shifter_1_out_2), .out_4(out_3), .in_3(in_2));
endmodule

module _2_bit_RS_with_ENB (
  input  [31:0] in_1,
  input  in_2,
  output [31:0] out_3
);

  wire [31:0] n2_bit_right_shifter_1_out_2;

  _2_bit_right_shifter u_2_bit_right_shifter_1 (.in_1(in_1), .out_2(n2_bit_right_shifter_1_out_2));
  _32_bit_num_select u_32_bit_num_select_1 (
    .in_1(in_1), .in_2(n2_bit_right_shifter_1_out_2), .out_4(out_3), .in_3(in_2));
endmodule

module _4_bit_RS_with_ENB (
  input  [31:0] in_1,
  input  in_2,
  output [31:0] out_3
);

  wire [31:0] n4_bit_right_shifter_1_out_2;

  _4_bit_right_shifter u_4_bit_right_shifter_1 (.in_1(in_1), .out_2(n4_bit_right_shifter_1_out_2));
  _32_bit_num_select u_32_bit_num_select_1 (
    .in_1(in_1), .in_2(n4_bit_right_shifter_1_out_2), .out_4(out_3), .in_3(in_2));
endmodule

module _8_bit_RS_with_ENB (
  input  [31:0] in_1,
  input  in_2,
  output [31:0] out_3
);

  wire [31:0] n8_bit_right_shifter_1_out_2;

  _8_bit_right_shifter u_8_bit_right_shifter_1 (.in_1(in_1), .out_2(n8_bit_right_shifter_1_out_2));
  _32_bit_num_select u_32_bit_num_select_1 (
    .in_1(in_1), .in_2(n8_bit_right_shifter_1_out_2), .out_4(out_3), .in_3(in_2));
endmodule

module _16_bit_RS_with_ENB (
  input  [31:0] in_1,
  input  in_2,
  output [31:0] out_3
);

  wire [31:0] n16_bit_right_shifter_1_out_2;

  _16_bit_right_shifter u_16_bit_right_shifter_1 (.in_1(in_1), .out_2(n16_bit_right_shifter_1_out_2));
  _32_bit_num_select u_32_bit_num_select_1 (
    .in_1(in_1), .in_2(n16_bit_right_shifter_1_out_2), .out_4(out_3), .in_3(in_2));
endmodule

module _1_bit_LS_with_ENB (
  input  [31:0] in_1,
  input  in_2,
  output [31:0] out_3
);

  wire [31:0] n1_bit_left_shifter_1_out_2;

  _1_bit_left_shifter u_1_bit_left_shifter_1 (.in_1(in_1), .out_2(n1_bit_left_shifter_1_out_2));
  _32_bit_num_select u_32_bit_num_select_1 (
    .in_1(in_1), .in_2(n1_bit_left_shifter_1_out_2), .out_4(out_3), .in_3(in_2));
endmodule

module _2_bit_LS_with_ENB (
  input  [31:0] in_1,
  input  in_2,
  output [31:0] out_3
);

  wire [31:0] n2_bit_left_shifter_1_out_2;

  _2_bit_left_shifter u_2_bit_left_shifter_1 (.in_1(in_1), .out_2(n2_bit_left_shifter_1_out_2));
  _32_bit_num_select u_32_bit_num_select_1 (
    .in_1(in_1), .in_2(n2_bit_left_shifter_1_out_2), .out_4(out_3), .in_3(in_2));
endmodule

module _4_bit_LS_with_ENB (
  input  [31:0] in_1,
  input  in_2,
  output [31:0] out_3
);

  wire [31:0] n4_bit_left_shifter_1_out_2;

  _4_bit_left_shifter u_4_bit_left_shifter_1 (.in_1(in_1), .out_2(n4_bit_left_shifter_1_out_2));
  _32_bit_num_select u_32_bit_num_select_1 (
    .in_1(in_1), .in_2(n4_bit_left_shifter_1_out_2), .out_4(out_3), .in_3(in_2));
endmodule

module _8_bit_LS_with_ENB (
  input  [31:0] in_1,
  input  in_2,
  output [31:0] out_3
);

  wire [31:0] n8_bit_left_shifter_1_out_2;

  _8_bit_left_shifter u_8_bit_left_shifter_1 (.in_1(in_1), .out_2(n8_bit_left_shifter_1_out_2));
  _32_bit_num_select u_32_bit_num_select_1 (
    .in_1(in_1), .in_2(n8_bit_left_shifter_1_out_2), .out_4(out_3), .in_3(in_2));
endmodule

module _16_bit_LS_with_ENB (
  input  [31:0] in_1,
  input  in_2,
  output [31:0] out_3
);

  wire [31:0] n16_bit_right_shifter_1_out_2;

  _16_bit_right_shifter u_16_bit_right_shifter_1 (.in_1(in_1), .out_2(n16_bit_right_shifter_1_out_2));
  _32_bit_num_select u_32_bit_num_select_1 (
    .in_1(in_1), .in_2(n16_bit_right_shifter_1_out_2), .out_4(out_3), .in_3(in_2));
endmodule

module ALU (
  input  [31:0] A,
  input  [31:0] B,
  input  [1:0] in_3,
  output [31:0] Out,
  output Ext
);

  wire Bout, Cout, Sign_Mag_Cout, Zero;
  wire [30:0] adder_2_out;
  wire [31:0] A_prime, bit_extender_1_out, bit_extender_2_out, bit_extender_3_out,
       n32_bit_num_select_1_out_4, n32_bit_num_select_2_out_4, negator_1_out, negator_2_out, negator_3_out,
       Sign_Mag_Add, Sub, Sum;
  wire [31:31] n32_bit_num_select_3_out_4;

  not not_1 (A_prime[0], A[0]);
  not not_2 (A_prime[1], A[1]);
  not not_3 (A_prime[2], A[2]);
  not not_4 (A_prime[3], A[3]);
  not not_5 (A_prime[4], A[4]);
  not not_6 (A_prime[5], A[5]);
  not not_7 (A_prime[6], A[6]);
  not not_8 (A_prime[7], A[7]);
  not not_9 (A_prime[8], A[8]);
  not not_10 (A_prime[9], A[9]);
  not not_11 (A_prime[10], A[10]);
  not not_12 (A_prime[11], A[11]);
  not not_13 (A_prime[12], A[12]);
  not not_14 (A_prime[13], A[13]);
  not not_15 (A_prime[14], A[14]);
  not not_16 (A_prime[15], A[15]);
  not not_17 (A_prime[16], A[16]);
  not not_18 (A_prime[17], A[17]);
  not not_19 (A_prime[18], A[18]);
  not not_20 (A_prime[19], A[19]);
  not not_21 (A_prime[20], A[20]);
  not not_22 (A_prime[21], A[21]);
  not not_23 (A_prime[22], A[22]);
  not not_24 (A_prime[23], A[23]);
  not not_25 (A_prime[24], A[24]);
  not not_26 (A_prime[25], A[25]);
  not not_27 (A_prime[26], A[26]);
  not not_28 (A_prime[27], A[27]);
  not not_29 (A_prime[28], A[28]);
  not not_30 (A_prime[29], A[29]);
  not not_31 (A_prime[30], A[30]);
  not not_32 (A_prime[31], A[31]);
  assign bit_extender_1_out = {{1{1'b0}}, A[30:0]};  // Bit_Extender bit_extender_1
  Negator #(.width(32)) negator_1 (.in(bit_extender_1_out), .out(negator_1_out));
  Negator #(.width(32)) negator_2 (.in(bit_extender_2_out), .out(negator_2_out));
  assign bit_extender_2_out = {{1{1'b0}}, B[30:0]};  // Bit_Extender bit_extender_2
  _32_bit_num_select u_32_bit_num_select_1 (
    .in_1(A), .in_2(negator_1_out), .out_4(n32_bit_num_select_1_out_4), .in_3(A[31]));
  _32_bit_num_select u_32_bit_num_select_2 (
    .in_1(B), .in_2(negator_2_out), .out_4(n32_bit_num_select_2_out_4), .in_3(B[31]));
  Adder #(.width(32)) adder_1 (.a(A), .b(B), .out(Sum), .cin(1'b0), .cout(Cout));
  Adder #(.width(32)) adder_2 (
    .a(n32_bit_num_select_1_out_4), .b(n32_bit_num_select_2_out_4), .out({Sign_Mag_Add[31], adder_2_out}),
    .cin(1'b0), .cout(Sign_Mag_Cout));
  or or_1 (Zero, A[0], A[1], A[2], A[3], A[4], A[5], A[6], A[7], A[8], A[9], A[10], A[11], A[12], A[13], A[14], A[15], A[16], A[17], A[18], A[19], A[20], A[21], A[22], A[23], A[24], A[25], A[26], A[27], A[28], A[29], A[30], A[31]);
  Subtractor #(.width(32)) subtractor_1 (.a(A), .b(B), .out(Sub), .bin(1'b0), .bout(Bout));
  assign bit_extender_3_out = {{1{1'b0}}, adder_2_out};  // Bit_Extender bit_extender_3
  Negator #(.width(32)) negator_3 (.in(bit_extender_3_out), .out(negator_3_out));
  _32_bit_num_select u_32_bit_num_select_3 (
    .in_1({Sign_Mag_Add[31], adder_2_out}), .in_2(negator_3_out),
    .out_4({n32_bit_num_select_3_out_4[31], Sign_Mag_Add[30:0]}), .in_3(Sign_Mag_Add[31]));
  Multiplexer #(.select(2), .width(32), .enable("false")) multiplexer_1 (
    .in0(Sum), .in1(Sub), .in2(A_prime), .in3(Sign_Mag_Add), .out(Out), .sel(in_3));
  Multiplexer #(.select(2), .enable("false")) multiplexer_2 (
    .in0(Cout), .in1(Bout), .in2(Zero), .in3(Sign_Mag_Cout), .out(Ext), .sel(in_3));

  // Other names for the same wires on the sheet: Select[1:0] = in_3
endmodule

module clamp_to_5_bit (
  input  [31:0] in_1,
  output [4:0] out_2
);

  wire alu_1_ext;
  wire [7:5] n8_bit_num_select_1_out_4;

  _8_bit_num_select u_8_bit_num_select_1 (
    .in_1(8'h1f), .in_2(in_1[7:0]), .out_4({n8_bit_num_select_1_out_4, out_2}), .in_3(alu_1_ext));
  ALU alu_1 (.A(in_1), .B(32'h1f), .in_3(2'b01), .Ext(alu_1_ext));  // open: Out
endmodule

module pick_sort (
  input  [31:0] A,
  input  [31:0] B,
  input  [10:0] KeyA,
  input  [10:0] KeyB,
  output [31:0] Smaller,
  output [31:0] Larger
);

  wire alu_1_ext;
  wire [31:0] bit_extender_1_out, bit_extender_2_out;

  assign bit_extender_1_out = {{21{1'b0}}, KeyA};  // Bit_Extender bit_extender_1
  assign bit_extender_2_out = {{21{1'b0}}, KeyB};  // Bit_Extender bit_extender_2
  _32_bit_num_select u_32_bit_num_select_1 (.in_1(A), .in_2(B), .out_4(Smaller), .in_3(alu_1_ext));
  _32_bit_num_select u_32_bit_num_select_2 (.in_1(B), .in_2(A), .out_4(Larger), .in_3(alu_1_ext));
  ALU alu_1 (.A(bit_extender_2_out), .B(bit_extender_1_out), .in_3(2'b01), .Ext(alu_1_ext));  // open: Out
endmodule

module float_dtor (
  input  [31:0] in_1,
  output Sign,
  output [10:0] Exponent,
  output [19:0] Significand
);


  assign Exponent = in_1[30:20];
  assign Sign = in_1[31];
  assign Significand = in_1[19:0];
endmodule

module float_ctor (
  input  Sign,
  input  [10:0] Exponent,
  input  [19:0] Significand,
  output [31:0] out_4
);


  assign out_4 = {Sign, Exponent, Significand};
endmodule

module truncator_23_to_21 (
  input  [22:0] X,
  output [20:0] Y
);

  wire n7408_1__3__1y, n7432_1__3__1y, n7432_1__6__2y;
  wire [31:0] bit_extender_1_out, bit_extender_2_out;
  wire [31:21] alu_1_out;

  _7432 u_7432_1 (
    ._1__1A(X[1]), ._2__1B(X[0]), ._3__1Y(n7432_1__3__1y), ._4__2A(n7432_1__3__1y), ._5__2B(X[3]),
    ._6__2Y(n7432_1__6__2y));  // open: _7__GND, _14__Vcc, _13__4B, _12__4A, _11__4Y, _10__3B, _9__3A, _8__3Y
  _7408 u_7408_1 (
    ._1__1A(X[2]), ._2__1B(n7432_1__6__2y), ._3__1Y(n7408_1__3__1y));  // open: _4__2A, _5__2B, _6__2Y, _7__GND, _14__Vcc, _13__4B, _12__4A, _11__4Y, _10__3B, _9__3A, _8__3Y
  assign bit_extender_1_out = {{12{1'b0}}, X[22:3]};  // Bit_Extender bit_extender_1
  assign bit_extender_2_out = {{31{1'b0}}, n7408_1__3__1y};  // Bit_Extender bit_extender_2
  ALU alu_1 (.A(bit_extender_2_out), .B(bit_extender_1_out), .in_3(2'b00), .Out({alu_1_out, Y}));  // open: Ext

  // Other names for the same wires on the sheet: S = X[0]; R = X[1]; G = X[2]; L = X[3]; N[19:0] = X[22:3]
endmodule

module _7408 (
  input  _1__1A,
  input  _14__Vcc,
  input  _2__1B,
  input  _13__4B,
  input  _12__4A,
  input  _4__2A,
  input  _5__2B,
  input  _10__3B,
  input  _9__3A,
  input  _7__GND,
  output _3__1Y,
  output _11__4Y,
  output _6__2Y,
  output _8__3Y
);

  and and_1 (_3__1Y, _2__1B, _1__1A);
  and and_2 (_6__2Y, _5__2B, _4__2A);
  and and_3 (_11__4Y, _13__4B, _12__4A);
  and and_4 (_8__3Y, _10__3B, _9__3A);

  // Notes on the sheet:
  //   7408: quad AND
endmodule

module _7432 (
  input  _1__1A,
  input  _14__Vcc,
  input  _2__1B,
  input  _13__4B,
  input  _12__4A,
  input  _4__2A,
  input  _5__2B,
  input  _10__3B,
  input  _9__3A,
  input  _7__GND,
  output _3__1Y,
  output _11__4Y,
  output _6__2Y,
  output _8__3Y
);

  or or_1 (_3__1Y, _2__1B, _1__1A);
  or or_2 (_6__2Y, _5__2B, _4__2A);
  or or_3 (_11__4Y, _13__4B, _12__4A);
  or or_4 (_8__3Y, _10__3B, _9__3A);

  // Notes on the sheet:
  //   7432: quad OR
endmodule

module float_ctor_with_grs (
  input  Sign,
  input  [10:0] Exponent,
  input  [19:0] Significand,
  input  [2:0] GRS,
  output [31:0] out_5,
  output Overflow
);

  wire alu_3_ext, n7404_1__2__1y;
  wire [20:0] truncator_23_to_21_1_y;
  wire [31:0] alu_1_out, alu_2_out, bit_extender_1_out, bit_extender_2_out, bit_extender_3_out;

  truncator_23_to_21 truncator_23_to_21_1 (.X({Significand, GRS}), .Y(truncator_23_to_21_1_y));
  assign bit_extender_1_out = {{21{1'b0}}, Exponent};  // Bit_Extender bit_extender_1
  assign bit_extender_2_out = {{31{1'b0}}, truncator_23_to_21_1_y[20]};  // Bit_Extender bit_extender_2
  ALU alu_1 (.A(bit_extender_2_out), .B(bit_extender_1_out), .in_3(2'b00), .Out(alu_1_out));  // open: Ext
  float_ctor float_ctor_1 (
    .out_4(out_5), .Sign(Sign), .Exponent(alu_1_out[10:0]), .Significand(truncator_23_to_21_1_y[19:0]));
  assign bit_extender_3_out = {{21{1'b1}}, alu_1_out[10:0]};  // Bit_Extender bit_extender_3
  ALU alu_2 (.A(bit_extender_3_out), .in_3(2'b10), .Out(alu_2_out));  // open: B, Ext
  ALU alu_3 (.A(alu_2_out), .in_3(2'b10), .Ext(alu_3_ext));  // open: B, Out
  _7404 u_7404_1 (
    ._1__1A(alu_3_ext), ._2__1Y(n7404_1__2__1y));  // open: _3__2A, _4__2Y, _5__3A, _6__3Y, _7__GND, _14__Vcc, _13__6A, _12__6Y, _11__5A, _10__5Y, _9__4A, _8__4Y
  _7432 u_7432_1 (
    ._1__1A(alu_1_out[11]), ._2__1B(n7404_1__2__1y), ._3__1Y(Overflow));  // open: _4__2A, _5__2B, _6__2Y, _7__GND, _14__Vcc, _13__4B, _12__4A, _11__4Y, _10__3B, _9__3A, _8__3Y
endmodule

module _74148 (
  input  _1__I4,
  input  _16__Vcc,
  input  _2__I5,
  input  _3__I6,
  input  _4__I7,
  input  _13__I3,
  input  _5__EI,
  input  _12__I2,
  input  _11__I1,
  input  _10__I0,
  input  _8__GND,
  output _15__EO,
  output _16__GS,
  output _6__A2,
  output _7__A1,
  output _9__A0
);

  wire not_1_out, not_2_out, not_3_out, not_4_out, not_5_out, not_6_out, not_7_out, not_8_out, not_9_out,
       not_10_out, not_11_out, not_12_out, priority_encoder_1_en_out, priority_encoder_1_gs;
  wire [2:0] priority_encoder_1_out;

  or or_1 (_16__GS, priority_encoder_1_en_out, _5__EI);
  not not_1 (not_1_out, _10__I0);
  not not_2 (not_2_out, _11__I1);
  not not_3 (not_3_out, _12__I2);
  not not_4 (not_4_out, _13__I3);
  Priority_Encoder #(.disabled(0)) priority_encoder_1 (
    .in0(not_1_out), .in1(not_2_out), .in2(not_3_out), .in3(not_4_out), .in4(not_5_out), .in5(not_6_out),
    .in6(not_7_out), .in7(not_8_out), .out(priority_encoder_1_out), .en_in(not_9_out),
    .gs(priority_encoder_1_gs), .en_out(priority_encoder_1_en_out));
  not not_5 (not_5_out, _1__I4);
  not not_6 (not_6_out, _2__I5);
  not not_7 (not_7_out, _3__I6);
  not not_8 (not_8_out, _4__I7);
  not not_9 (not_9_out, _5__EI);
  or or_2 (_15__EO, priority_encoder_1_gs, _5__EI);
  not not_10 (not_10_out, priority_encoder_1_out[0]);
  not not_11 (not_11_out, priority_encoder_1_out[1]);
  not not_12 (not_12_out, priority_encoder_1_out[2]);
  or or_3 (_9__A0, not_10_out, _16__GS);
  or or_4 (_7__A1, not_11_out, _16__GS);
  or or_5 (_6__A2, not_12_out, _16__GS);

  // Other names for the same wires on the sheet: A0 = _9__A0; A1 = _7__A1; A2 = _6__A2; E = _5__EI; EO = _15__EO;
  //   GS = _16__GS; I0 = _10__I0; I1 = _11__I1; I2 = _12__I2; I3 = _13__I3; I4 = _1__I4; I5 = _2__I5; I6 = _3__I6;
  //   I7 = _4__I7

  // Notes on the sheet:
  //   _8__GND: pull=down
  //   _16__Vcc: pull=up
  //   74148: 8-Line to 4-Line Priority Encoder
endmodule

module _8x3_pri_encoder (
  input  EI,
  input  [7:0] in_2,
  output GS,
  output [2:0] out_4,
  output EO
);

  _74148 u_74148_1 (
    ._1__I4(in_2[4]), ._2__I5(in_2[5]), ._3__I6(in_2[6]), ._4__I7(in_2[7]), ._5__EI(EI), ._6__A2(out_4[2]),
    ._7__A1(out_4[1]), ._15__EO(EO), ._16__GS(GS), ._13__I3(in_2[3]), ._12__I2(in_2[2]), ._11__I1(in_2[1]),
    ._10__I0(in_2[0]), ._9__A0(out_4[0]));  // open: _8__GND, _16__Vcc
endmodule

module _4_bit_bitwise_AND (
  input  [3:0] in_1,
  input  [3:0] in_2,
  output [3:0] out_3
);

  _7408 u_7408_1 (
    ._1__1A(in_1[0]), ._2__1B(in_2[0]), ._3__1Y(out_3[0]), ._4__2A(in_1[1]), ._5__2B(in_2[1]),
    ._6__2Y(out_3[1]), ._13__4B(in_2[3]), ._12__4A(in_1[3]), ._11__4Y(out_3[3]), ._10__3B(in_2[2]),
    ._9__3A(in_1[2]), ._8__3Y(out_3[2]));  // open: _7__GND, _14__Vcc
endmodule

module _5_bit_bitwise_AND (
  input  [4:0] in_1,
  input  [4:0] in_2,
  output [4:0] out_3
);

  wire [3:1] n4_bit_bitwise_and_2_out_3;
  wire [7:0] bit_extender_1_out, bit_extender_2_out;

  assign bit_extender_1_out = {{3{1'b0}}, in_1};  // Bit_Extender bit_extender_1
  assign bit_extender_2_out = {{3{1'b0}}, in_2};  // Bit_Extender bit_extender_2
  _4_bit_bitwise_AND u_4_bit_bitwise_and_1 (
    .in_1(bit_extender_1_out[3:0]), .in_2(bit_extender_2_out[3:0]), .out_3(out_3[3:0]));
  _4_bit_bitwise_AND u_4_bit_bitwise_and_2 (
    .in_1(bit_extender_1_out[7:4]), .in_2(bit_extender_2_out[7:4]),
    .out_3({n4_bit_bitwise_and_2_out_3, out_3[4]}));
endmodule

module _16x4_pri_encoder (
  input  EI,
  input  [15:0] in_2,
  output GS,
  output [3:0] O,
  output EO
);

  wire n8x3_pri_encoder_1_eo;
  wire [2:0] n8x3_pri_encoder_1_out_4, n8x3_pri_encoder_2_out_4;
  wire [3:3] n8x3_pri_encoder_2_gs;

  _8x3_pri_encoder u_8x3_pri_encoder_1 (
    .EI(EI), .in_2(in_2[15:8]), .GS(O[3]), .out_4(n8x3_pri_encoder_1_out_4), .EO(n8x3_pri_encoder_1_eo));
  _8x3_pri_encoder u_8x3_pri_encoder_2 (
    .EI(n8x3_pri_encoder_1_eo), .in_2(in_2[7:0]), .GS(n8x3_pri_encoder_2_gs[3]),
    .out_4(n8x3_pri_encoder_2_out_4), .EO(EO));
  _4_bit_bitwise_AND u_4_bit_bitwise_and_1 (
    .in_1({O[3], n8x3_pri_encoder_1_out_4}), .in_2({n8x3_pri_encoder_2_gs[3], n8x3_pri_encoder_2_out_4}),
    .out_3({GS, O[2:0]}));
endmodule

module _32x5_pri_encoder (
  input  EI,
  input  [31:0] in_2,
  output GS,
  output [4:0] O,
  output EO
);

  wire n16x4_pri_encoder_1_eo;
  wire [3:0] n16x4_pri_encoder_1_o, n16x4_pri_encoder_2_o;
  wire [4:4] n16x4_pri_encoder_2_gs;

  _16x4_pri_encoder u_16x4_pri_encoder_1 (
    .EI(EI), .in_2(in_2[31:16]), .GS(O[4]), .O(n16x4_pri_encoder_1_o), .EO(n16x4_pri_encoder_1_eo));
  _16x4_pri_encoder u_16x4_pri_encoder_2 (
    .EI(n16x4_pri_encoder_1_eo), .in_2(in_2[15:0]), .GS(n16x4_pri_encoder_2_gs[4]),
    .O(n16x4_pri_encoder_2_o), .EO(EO));
  _5_bit_bitwise_AND u_5_bit_bitwise_and_1 (
    .in_1({O[4], n16x4_pri_encoder_1_o}), .in_2({n16x4_pri_encoder_2_gs[4], n16x4_pri_encoder_2_o}),
    .out_3({GS, O[3:0]}));
endmodule

module LS_Normalizer (
  input  [1:0] Pre_Radix,
  input  [10:0] Exponent,
  input  [19:0] Significand,
  input  [2:0] GRS,
  output Underflow,
  output [1:0] new_Pre_Radix,
  output [10:0] new_Exponent,
  output [19:0] new_Significant,
  output [2:0] new_GRS
);

  wire [4:0] n32x5_pri_with_high_in_1_out_2;
  wire [31:0] alu_1_out, bit_extender_1_out, bit_extender_2_out, bit_extender_3_out, bit_extender_4_out;
  wire [31:11] alu_2_out;
  wire [31:25] ls_upto_31_bit_1_y;

  _32x5_pri_with_high_in u_32x5_pri_with_high_in_1 (
    .in_1({Significand, GRS, {9{1'b0}}}), .out_2(n32x5_pri_with_high_in_1_out_2));
  assign bit_extender_1_out = {{21{1'b0}}, Exponent};  // Bit_Extender bit_extender_1
  assign bit_extender_2_out = {{27{1'b0}}, n32x5_pri_with_high_in_1_out_2};  // Bit_Extender bit_extender_2
  assign bit_extender_3_out = {{7{1'b0}}, {Pre_Radix, Significand, GRS}};  // Bit_Extender bit_extender_3
  ALU alu_1 (.A(bit_extender_2_out), .B(32'h1), .in_3(2'b00), .Out(alu_1_out));  // open: Ext
  LS__upto_31_bit ls_upto_31_bit_1 (
    .X(bit_extender_3_out), .Amt(alu_1_out), .Y({ls_upto_31_bit_1_y, new_Pre_Radix, new_Significant, new_GRS}));
  assign bit_extender_4_out = {{27{1'b0}}, alu_1_out[4:0]};  // Bit_Extender bit_extender_4
  ALU alu_2 (
    .A(bit_extender_1_out), .B(bit_extender_4_out), .in_3(2'b01), .Out({alu_2_out, new_Exponent}),
    .Ext(Underflow));
endmodule

module RS__upto_31_bit (
  input  [31:0] X,
  input  [31:0] Amt,
  output [31:0] Y
);

  wire [4:0] clamp_to_5_bit_1_out_2;
  wire [31:0] n2_bit_rs_with_enb_1_out_3, n4_bit_rs_with_enb_1_out_3, n8_bit_rs_with_enb_1_out_3,
       n16_bit_rs_with_enb_1_out_3;

  _16_bit_RS_with_ENB u_16_bit_rs_with_enb_1 (
    .in_1(X), .out_3(n16_bit_rs_with_enb_1_out_3), .in_2(clamp_to_5_bit_1_out_2[4]));
  _8_bit_RS_with_ENB u_8_bit_rs_with_enb_1 (
    .in_1(n16_bit_rs_with_enb_1_out_3), .out_3(n8_bit_rs_with_enb_1_out_3), .in_2(clamp_to_5_bit_1_out_2[3]));
  clamp_to_5_bit clamp_to_5_bit_1 (.in_1(Amt), .out_2(clamp_to_5_bit_1_out_2));
  _4_bit_RS_with_ENB u_4_bit_rs_with_enb_1 (
    .in_1(n8_bit_rs_with_enb_1_out_3), .out_3(n4_bit_rs_with_enb_1_out_3), .in_2(clamp_to_5_bit_1_out_2[2]));
  _2_bit_RS_with_ENB u_2_bit_rs_with_enb_1 (
    .in_1(n4_bit_rs_with_enb_1_out_3), .out_3(n2_bit_rs_with_enb_1_out_3), .in_2(clamp_to_5_bit_1_out_2[1]));
  _1_bit_RS_with_ENB u_1_bit_rs_with_enb_1 (
    .in_1(n2_bit_rs_with_enb_1_out_3), .out_3(Y), .in_2(clamp_to_5_bit_1_out_2[0]));
endmodule

module LS__upto_31_bit (
  input  [31:0] X,
  input  [31:0] Amt,
  output [31:0] Y
);

  wire [4:0] clamp_to_5_bit_1_out_2;
  wire [31:0] n2_bit_ls_with_enb_1_out_3, n4_bit_ls_with_enb_1_out_3, n8_bit_ls_with_enb_1_out_3,
       n16_bit_ls_with_enb_1_out_3;

  _16_bit_LS_with_ENB u_16_bit_ls_with_enb_1 (
    .in_1(X), .out_3(n16_bit_ls_with_enb_1_out_3), .in_2(clamp_to_5_bit_1_out_2[4]));
  _8_bit_LS_with_ENB u_8_bit_ls_with_enb_1 (
    .in_1(n16_bit_ls_with_enb_1_out_3), .out_3(n8_bit_ls_with_enb_1_out_3), .in_2(clamp_to_5_bit_1_out_2[3]));
  clamp_to_5_bit clamp_to_5_bit_1 (.in_1(Amt), .out_2(clamp_to_5_bit_1_out_2));
  _4_bit_LS_with_ENB u_4_bit_ls_with_enb_1 (
    .in_1(n8_bit_ls_with_enb_1_out_3), .out_3(n4_bit_ls_with_enb_1_out_3), .in_2(clamp_to_5_bit_1_out_2[2]));
  _2_bit_LS_with_ENB u_2_bit_ls_with_enb_1 (
    .in_1(n4_bit_ls_with_enb_1_out_3), .out_3(n2_bit_ls_with_enb_1_out_3), .in_2(clamp_to_5_bit_1_out_2[1]));
  _1_bit_LS_with_ENB u_1_bit_ls_with_enb_1 (
    .in_1(n2_bit_ls_with_enb_1_out_3), .in_2(clamp_to_5_bit_1_out_2[0]), .out_3(Y));
endmodule

module RS_Normalizer (
  input  [1:0] Pre_Radix,
  input  [10:0] Exponent,
  input  [19:0] Significand,
  input  [2:0] GRS,
  output Overflow,
  output [1:0] new_Pre_Radix,
  output [10:0] new_Exponent,
  output [19:0] new_Significant,
  output [2:0] new_GRS
);

  wire [31:0] bit_extender_1_out, bit_extender_2_out;
  wire [31:12] alu_1_out;
  wire [31:25] n1_bit_right_shifter_1_out_2;

  assign bit_extender_1_out = {{21{1'b0}}, Exponent};  // Bit_Extender bit_extender_1
  assign bit_extender_2_out = {{7{1'b0}}, {Pre_Radix, Significand, GRS}};  // Bit_Extender bit_extender_2
  ALU alu_1 (.A(32'h1), .B(bit_extender_1_out), .in_3(2'b00), .Out({alu_1_out, Overflow, new_Exponent}));  // open: Ext
  _1_bit_right_shifter u_1_bit_right_shifter_1 (
    .in_1(bit_extender_2_out), .out_2({n1_bit_right_shifter_1_out_2, new_Pre_Radix, new_Significant, new_GRS}));
endmodule

module Normalizer (
  input  [1:0] Pre_Radix,
  input  [10:0] Expoonent,
  input  [19:0] Significand,
  input  [2:0] GRS,
  output Norm_Overflow,
  output [1:0] Norm_Pre_Radix,
  output [2:0] Norm_GRS,
  output Norm_Underflow,
  output [19:0] Norm_Significand,
  output [10:0] Norm_Exponent
);

  wire Already_Normalized, alu_1_ext, LS_Normalization;
  wire [1:0] LS_Pre_Radix, RS_Pre_Radix;
  wire [2:0] LS_GRS, RS_GRS;
  wire [5:5] LS_PRGRSU;
  wire [7:0] bit_extender_1_out, bit_extender_2_out, bit_extender_5_out, n8_bit_num_select_1_out_4;
  wire [7:6] Norm_PRGRS;
  wire [10:0] LS_Exponent, Norm_Exp, RS_Exponent;
  wire [15:0] bit_extender_3_out;
  wire [15:11] n16_bit_num_select_1_out_4;
  wire [19:0] LS_OES;
  wire [31:0] bit_extender_4_out, n32_bit_num_select_1_out_4, RS_OES;

  _74139 u_74139_1 (
    ._1__1G(1'b0), ._2__1A(Pre_Radix[0]), ._3__1B(Pre_Radix[1]), ._4__1Y0(LS_Normalization),
    ._5__1Y1(Already_Normalized));  // open: _6__1Y2, _7__1Y3, _8__GND, _16__Vcc, _15__2G, _14__2A, _13__2B, _12__2Y0, _11__2Y1, _10__2Y2, _9__2Y3
  _32_bit_num_select u_32_bit_num_select_1 (
    .in_1({1'b0, Expoonent, Significand}), .in_2({RS_OES[31], RS_Exponent, RS_OES[19:0]}),
    .out_4(n32_bit_num_select_1_out_4), .in_3(Already_Normalized));
  _32_bit_num_select u_32_bit_num_select_2 (
    .in_1({1'b0, LS_Exponent, LS_OES}), .in_2(n32_bit_num_select_1_out_4),
    .out_4({Norm_Overflow, Norm_Exp, Norm_Significand}), .in_3(LS_Normalization));
  LS_Normalizer ls_normalizer_1 (
    .Pre_Radix(Pre_Radix), .Exponent(Expoonent), .Significand(Significand), .GRS(GRS),
    .Underflow(LS_PRGRSU[5]), .new_Pre_Radix(LS_Pre_Radix), .new_Exponent(LS_Exponent),
    .new_Significant(LS_OES), .new_GRS(LS_GRS));
  RS_Normalizer rs_normalizer_1 (
    .Pre_Radix(Pre_Radix), .Exponent(Expoonent), .Significand(Significand), .GRS(GRS), .Overflow(RS_OES[31]),
    .new_Pre_Radix(RS_Pre_Radix), .new_Exponent(RS_Exponent), .new_Significant(RS_OES[19:0]), .new_GRS(RS_GRS));
  assign bit_extender_1_out = {{2{1'b0}}, {1'b0, GRS, Pre_Radix}};  // Bit_Extender bit_extender_1
  assign bit_extender_2_out = {{2{1'b0}}, {1'b0, RS_GRS, RS_Pre_Radix}};  // Bit_Extender bit_extender_2
  assign bit_extender_3_out = {{5{1'b0}}, Norm_Exp};  // Bit_Extender bit_extender_3
  assign bit_extender_4_out = {{4{1'b0}}, {Norm_PRGRS, Norm_Underflow, Norm_GRS, Norm_Pre_Radix, Norm_Significand}};  // Bit_Extender bit_extender_4
  _16_bit_num_select u_16_bit_num_select_1 (
    .in_1({16{1'b0}}), .in_2(bit_extender_3_out), .out_4({n16_bit_num_select_1_out_4, Norm_Exponent}),
    .in_3(alu_1_ext));
  ALU alu_1 (.A(bit_extender_4_out), .in_3(2'b10), .Ext(alu_1_ext));  // open: B, Out
  _8_bit_num_select u_8_bit_num_select_1 (
    .in_1(bit_extender_1_out), .in_2(bit_extender_2_out), .out_4(n8_bit_num_select_1_out_4),
    .in_3(Already_Normalized));
  assign bit_extender_5_out = {{2{1'b0}}, {LS_PRGRSU[5], LS_GRS, LS_Pre_Radix}};  // Bit_Extender bit_extender_5
  _8_bit_num_select u_8_bit_num_select_2 (
    .in_1(bit_extender_5_out), .in_2(n8_bit_num_select_1_out_4),
    .out_4({Norm_PRGRS, Norm_Underflow, Norm_GRS, Norm_Pre_Radix}), .in_3(LS_Normalization));

  // Other names for the same wires on the sheet: Norm_Sig[19:0] = Norm_Significand;
  //   Norm_PRGRS[5:0] = {Norm_Underflow, Norm_GRS, Norm_Pre_Radix}; LS_Significand[19:0] = LS_OES;
  //   LS_OES[30:20] = LS_Exponent; LS_PRGRSU[4:0] = {LS_GRS, LS_Pre_Radix}; LS_Underflow = LS_PRGRSU[5];
  //   OES[30:0] = {Expoonent, Significand}; Exponent[10:0] = Expoonent; PRGRSU[4:0] = {GRS, Pre_Radix};
  //   RS_Significand[19:0] = RS_OES[19:0]; RS_OES[30:20] = RS_Exponent; RS_Overflow = RS_OES[31];
  //   RS_PRGRSU[4:0] = {RS_GRS, RS_Pre_Radix}
endmodule

module _74139 (
  input  _1__1G,
  input  _16__Vcc,
  input  _2__1A,
  input  _15__2G,
  input  _3__1B,
  input  _14__2A,
  input  _13__2B,
  input  _8__GND,
  output _4__1Y0,
  output _5__1Y1,
  output _12__2Y0,
  output _6__1Y2,
  output _11__2Y1,
  output _7__1Y3,
  output _10__2Y2,
  output _9__2Y3
);

  wire decoder_1_out0, decoder_1_out1, decoder_1_out2, decoder_1_out3, decoder_2_out0, decoder_2_out1,
       decoder_2_out2, decoder_2_out3, not_1_out, not_2_out, not_3_out, not_4_out, not_5_out, not_6_out,
       not_7_out, not_8_out, not_9_out, not_10_out;

  not not_1 (not_1_out, _1__1G);
  and and_1 (_4__1Y0, not_1_out, not_2_out);
  not not_2 (not_2_out, decoder_1_out0);
  and and_2 (_5__1Y1, not_1_out, not_3_out);
  not not_3 (not_3_out, decoder_1_out1);
  and and_3 (_6__1Y2, not_1_out, not_4_out);
  not not_4 (not_4_out, decoder_1_out2);
  and and_4 (_7__1Y3, not_1_out, not_5_out);
  not not_5 (not_5_out, decoder_1_out3);
  Decoder #(.select(2), .enable("false")) decoder_1 (
    .out0(decoder_1_out0), .out1(decoder_1_out1), .out2(decoder_1_out2), .out3(decoder_1_out3),
    .sel({_3__1B, _2__1A}));
  Decoder #(.select(2), .enable("false")) decoder_2 (
    .out0(decoder_2_out0), .out1(decoder_2_out1), .out2(decoder_2_out2), .out3(decoder_2_out3),
    .sel({_13__2B, _14__2A}));
  not not_6 (not_6_out, _15__2G);
  not not_7 (not_7_out, decoder_2_out0);
  not not_8 (not_8_out, decoder_2_out1);
  not not_9 (not_9_out, decoder_2_out2);
  not not_10 (not_10_out, decoder_2_out3);
  and and_5 (_12__2Y0, not_6_out, not_7_out);
  and and_6 (_11__2Y1, not_6_out, not_8_out);
  and and_7 (_10__2Y2, not_6_out, not_9_out);
  and and_8 (_9__2Y3, not_6_out, not_10_out);

  // Notes on the sheet:
  //   74139: Dual 2-Line to 4-Line Decoder
endmodule

module _32x5_pri_with_high_in (
  input  [31:0] in_1,
  output [4:0] out_2
);

  wire [31:0] alu_1_out;

  ALU alu_1 (.A(in_1), .in_3(2'b10), .Out(alu_1_out));  // open: B, Ext
  _32x5_pri_encoder u_32x5_pri_encoder_1 (.EI(1'b0), .in_2(alu_1_out), .O(out_2));  // open: GS, EO
endmodule

module exp_equalizer (
  input  [31:0] in_1,
  input  [31:0] in_2,
  output L_Sign,
  output S_Sign,
  output [10:0] L_Exponent,
  output [10:0] S_Exponent,
  output [19:0] L_Significand,
  output [2:0] L_GRS,
  output S_Pre_Radix,
  output L_Pre_Radix,
  output [19:0] S_Significand,
  output [2:0] S_GRS
);

  wire R_PR;
  wire [10:0] float_dtor_1_exponent, float_dtor_2_exponent, float_dtor_4_exponent;
  wire [19:0] float_dtor_4_significand;
  wire [31:0] alu_1_out, bit_extender_3_out, L_E, pick_sort_1_larger, pick_sort_1_smaller, R_E;
  wire [31:24] rs_upto_31_bit_1_y;

  float_dtor float_dtor_1 (.in_1(in_1), .Exponent(float_dtor_1_exponent));  // open: Sign, Significand
  float_dtor float_dtor_2 (.in_1(in_2), .Exponent(float_dtor_2_exponent));  // open: Sign, Significand
  float_dtor float_dtor_3 (
    .in_1(pick_sort_1_larger), .Sign(L_Sign), .Exponent(L_Exponent), .Significand(L_Significand));
  pick_sort pick_sort_1 (
    .A(in_1), .B(in_2), .KeyA(float_dtor_1_exponent), .KeyB(float_dtor_2_exponent),
    .Smaller(pick_sort_1_smaller), .Larger(pick_sort_1_larger));
  assign L_E = {{21{1'b0}}, L_Exponent};  // Bit_Extender bit_extender_1
  ALU alu_1 (.A(L_E), .B(R_E), .in_3(2'b01), .Out(alu_1_out));  // open: Ext
  float_dtor float_dtor_4 (
    .in_1(pick_sort_1_smaller), .Sign(S_Sign), .Exponent(float_dtor_4_exponent),
    .Significand(float_dtor_4_significand));
  assign R_E = {{21{1'b0}}, float_dtor_4_exponent};  // Bit_Extender bit_extender_2
  assign bit_extender_3_out = {{8{1'b0}}, {R_PR, float_dtor_4_significand, 3'b000}};  // Bit_Extender bit_extender_3
  ALU alu_2 (.A(L_E), .in_3(2'b10), .Ext(L_Pre_Radix));  // open: B, Out
  RS__upto_31_bit rs_upto_31_bit_1 (
    .X(bit_extender_3_out), .Amt(alu_1_out), .Y({rs_upto_31_bit_1_y, S_Pre_Radix, S_Significand, S_GRS}));
  ALU alu_3 (.A(R_E), .in_3(2'b10), .Ext(R_PR));  // open: B, Out

  assign L_GRS = 3'b000;
  assign S_Exponent = L_Exponent;

  // Other names for the same wires on the sheet: L_PR = L_Pre_Radix
endmodule

module FPA (
  input  [31:0] A,
  input  [31:0] B,
  output Underflow,
  output Overflow,
  output [31:0] F
);

  wire float_ctor_with_grs_1_overflow, normalizer_1_norm_overflow;
  wire [2:0] exp_equalizer_1_l_grs, exp_equalizer_1_s_grs, normalizer_1_norm_grs;
  wire [10:0] exp_equalizer_1_l_exponent, normalizer_1_norm_exponent;
  wire [19:0] exp_equalizer_1_l_significand, exp_equalizer_1_s_significand, normalizer_1_norm_significand;
  wire [31:0] alu_1_out;
  wire [31:23] exp_equalizer_1_l_pre_radix, exp_equalizer_1_s_pre_radix;

  exp_equalizer exp_equalizer_1 (
    .in_1(A), .in_2(B), .L_GRS(exp_equalizer_1_l_grs), .L_Sign(exp_equalizer_1_l_pre_radix[31]),
    .S_Sign(exp_equalizer_1_s_pre_radix[31]), .L_Exponent(exp_equalizer_1_l_exponent),
    .S_Significand(exp_equalizer_1_s_significand), .S_GRS(exp_equalizer_1_s_grs),
    .L_Significand(exp_equalizer_1_l_significand), .L_Pre_Radix(exp_equalizer_1_l_pre_radix[23]),
    .S_Pre_Radix(exp_equalizer_1_s_pre_radix[23]));  // open: S_Exponent
  ALU alu_1 (
    .A({exp_equalizer_1_s_pre_radix[31], {7{1'b0}}, exp_equalizer_1_s_pre_radix[23], exp_equalizer_1_s_significand, exp_equalizer_1_s_grs}),
    .B({exp_equalizer_1_l_pre_radix[31], {7{1'b0}}, exp_equalizer_1_l_pre_radix[23], exp_equalizer_1_l_significand, exp_equalizer_1_l_grs}),
    .in_3(2'b11), .Out(alu_1_out));  // open: Ext
  Normalizer normalizer_1 (
    .Pre_Radix(alu_1_out[24:23]), .Expoonent(exp_equalizer_1_l_exponent), .Significand(alu_1_out[22:3]),
    .GRS(alu_1_out[2:0]), .Norm_Overflow(normalizer_1_norm_overflow), .Norm_GRS(normalizer_1_norm_grs),
    .Norm_Significand(normalizer_1_norm_significand), .Norm_Exponent(normalizer_1_norm_exponent),
    .Norm_Underflow(Underflow));  // open: Norm_Pre_Radix
  float_ctor_with_grs float_ctor_with_grs_1 (
    .Sign(alu_1_out[31]), .Exponent(normalizer_1_norm_exponent), .Significand(normalizer_1_norm_significand),
    .GRS(normalizer_1_norm_grs), .out_5(F), .Overflow(float_ctor_with_grs_1_overflow));
  _7432 u_7432_1 (
    ._1__1A(normalizer_1_norm_overflow), ._2__1B(float_ctor_with_grs_1_overflow), ._3__1Y(Overflow));  // open: _4__2A, _5__2B, _6__2Y, _7__GND, _14__Vcc, _13__4B, _12__4A, _11__4Y, _10__3B, _9__3A, _8__3Y
endmodule

module main (
  input  [31:0] A,
  input  [31:0] B,
  output Underflow,
  output Overflow,
  output [31:0] A_B
);

  FPA fpa_1 (.A(A), .B(B), .Overflow(Overflow), .F(A_B), .Underflow(Underflow));
endmodule

module _7404 (
  input  _1__1A,
  input  _14__Vcc,
  input  _13__6A,
  input  _3__2A,
  input  _11__5A,
  input  _5__3A,
  input  _9__4A,
  input  _7__GND,
  output _2__1Y,
  output _12__6Y,
  output _4__2Y,
  output _10__5Y,
  output _6__3Y,
  output _8__4Y
);

  not not_1 (_2__1Y, _1__1A);
  not not_2 (_4__2Y, _3__2A);
  not not_3 (_6__3Y, _5__3A);
  not not_4 (_12__6Y, _13__6A);
  not not_5 (_10__5Y, _11__5A);
  not not_6 (_8__4Y, _9__4A);

  // Notes on the sheet:
  //   7407: hex inverter
endmodule
